# Fritzing sketch LedSwitchPullup (saved by Fritzing 0.9.6b)
breadboards: 1

parts:
  Part1 = Arduino Uno (Rev3)
  S1 = Pushbutton [package="[THT]"]
  LED1 = LED - 5mm [color="Red (633nm)" current=0.030 package="5 mm [THT]"]
  R1 = Resistor [tolerance=±5% power=0.25 resistance=560 package=THT]

nets:
  N1: Part1.D8, S1.Pin_1, S1.Pin_2
  N2: Part1.D13/SCK, R1.Pin_0
  N3: Part1.GND, S1.Pin_3, S1.Pin_4, LED1.cathode
  N4: LED1.anode, R1.Pin_1

notes:
  R1 560R
  D13/PB5
  D8/PB0
  5V
  GND
  LED1
