# Fritzing sketch LSL_LSR (saved by Fritzing 1.0.3b)
breadboards: 1

parts:
  Part1 = Arduino Uno (Rev3)
  LED1 = LED - 5mm [color="Red (633nm)" current=0.030A package="5 mm [THT]"]
  LED2 = LED - 5mm [color="Red (633nm)" current=0.030A package="5 mm [THT]"]
  LED3 = LED - 5mm [color="Red (633nm)" current=0.030A package="5 mm [THT]"]
  LED4 = LED - 5mm [color="Red (633nm)" current=0.030A package="5 mm [THT]"]
  LED5 = LED - 5mm [color="Red (633nm)" current=0.030A package="5 mm [THT]"]
  LED6 = LED - 5mm [color="Red (633nm)" current=0.030A package="5 mm [THT]"]
  LED7 = LED - 5mm [color="Red (633nm)" current=0.030A package="5 mm [THT]"]
  R1 = Resistor [tolerance=±5% power=0.25W resistance=560 package=THT]
  R2 = Resistor [tolerance=±5% power=0.25W resistance=560 package=THT]
  R3 = Resistor [tolerance=±5% power=0.25W resistance=560 package=THT]
  R4 = Resistor [tolerance=±5% power=0.25W resistance=560 package=THT]
  R5 = Resistor [tolerance=±5% power=0.25W resistance=560 package=THT]
  R6 = Resistor [tolerance=±5% power=0.25W resistance=560 package=THT]
  R7 = Resistor [tolerance=±5% power=0.25W resistance=560 package=THT]
  LED8 = LED - 5mm [color="Red (633nm)" current=0.030A package="5 mm [THT]"]
  R8 = Resistor [tolerance=±5% power=0.25W resistance=560 package=THT]

nets:
  N1: Part1.GND, LED1.cathode, LED2.cathode, LED3.cathode, LED4.cathode, LED5.cathode, LED6.cathode, LED7.cathode, LED8.cathode
  N2: Part1.D0/RX, R8.Pin_1
  N3: Part1.D1/TX, R7.Pin_1
  N4: Part1.D2, R6.Pin_1
  N5: Part1.D3_PWM, R5.Pin_1
  N6: Part1.D4, R4.Pin_1
  N7: Part1.D5_PWM, R3.Pin_1
  N8: Part1.D6_PWM, R2.Pin_1
  N9: Part1.D7, R1.Pin_1
  N10: LED1.anode, R1.Pin_0
  N11: LED2.anode, R2.Pin_0
  N12: LED3.anode, R3.Pin_0
  N13: LED4.anode, R4.Pin_0
  N14: LED5.anode, R5.Pin_0
  N15: LED6.anode, R6.Pin_0
  N16: LED7.anode, R7.Pin_0
  N17: LED8.anode, R8.Pin_0

notes:
  D0
  D7
  GND
  Resistors all 560 Ω.
