# Fritzing sketch OR_AND (saved by Fritzing 1.0.3b)
breadboards: 1

parts:
  Part1 = Arduino Uno (Rev3)
  R1 = Resistor [tolerance=±5% power=0.25W resistance=10k package=THT]
  R2 = Resistor [tolerance=±5% power=0.25W resistance=10k package=THT]
  C1 = Ceramic Capacitor [capacitance=100nF voltage=35V package="100 mil [THT, multilayer]"]
  S1 = Pushbutton [package="[THT]"]
  LED1 = LED - 5mm [color="Red (633nm)" current=0.030A package="5 mm [THT]"]
  R3 = Resistor [tolerance=±5% power=0.25W resistance="560 " package=THT]

nets:
  N1: Part1.D9_PWM, R3.Pin_1
  N2: Part1.D11_PWM/MOSI, R2.Pin_1, C1.1
  N3: Part1.GND, S1.Pin_1, S1.Pin_2, LED1.cathode
  N4: Part1.5V, R1.Pin_0
  N5: R1.Pin_1, R2.Pin_0, S1.Pin_3, S1.Pin_4
  N6: LED1.anode, R3.Pin_0

notes:
  R1, R2 = 10 kΩ
  R3 = 560 Ω
  C1 = 100 nF
  SW1
  LED
  5V
  GND
  Pink  D9/PB1
  Yellow  D11/PB3
  Remove red 5V wire and its Resistor if using internal pullups.
