# Fritzing sketch AnalogInputOutput (saved by Fritzing 1.0.3b)
breadboards: 1

parts:
  Part1 = Arduino Uno (Rev3)
  R1 = Rotary Potentiometer (Small) [maximum_resistance=100kΩ knob_status=50% power=0.5W package=THT]
  LED1 = LED - 5mm [color="Red (633nm)" current=0.030A package="5 mm [THT]"]
  R2 = Resistor [tolerance=±5% power=0.25W resistance=560 package=THT]

nets:
  N1: Part1.A0, R1.wiper
  N2: Part1.D9_PWM, R2.Pin_0
  N3: Part1.5V, R1.leg1
  N4: Part1.GND, R1.leg2, LED1.cathode
  N5: LED1.anode, R2.Pin_1

notes:
  A0
  5V
  GND
  D9
  R1 = 560Ω
  LED1
  VR1 = 10KΩ
