# Fritzing sketch AnalogOutput (saved by Fritzing 1.0.3b)
breadboards: 1

parts:
  Part1 = Arduino Uno (Rev3)
  LED1 = LED - 5mm [color="Red (633nm)" current=0.030A package="5 mm [THT]"]
  R2 = Resistor [tolerance=±5% power=0.25W resistance=560 package=THT]

nets:
  N1: Part1.D9_PWM, R2.Pin_0
  N2: Part1.GND, LED1.cathode
  N3: LED1.anode, R2.Pin_1

notes:
  GND
  D9
  R1 = 560Ω
  LED1
