# Fritzing sketch Atmega328P_Pin_Capacitance (saved by Fritzing 1.0.3b)
breadboards: 1

parts:
  D1 = Rectifier Diode 10A [part_number=P1000K]
  D2 = Rectifier Diode 10A [part_number=P1000K]
  C_pin = Ceramic Capacitor [capacitance=10pF voltage=35V package="100 mil [THT, multilayer]"]
  Logic = longpad pin header, 1 pin [form="long pad"]
  R_pullup = Resistor [tolerance=±5% power=0.25W resistance=220 package=THT]
  5V = longpad pin header, 1 pin [form="long pad"]
  5V_2 = longpad pin header, 1 pin [form="long pad"]

nets:
  N1: D1.cathode, 5V.pin1
  Pin: D1.anode, D2.cathode, C_pin.1, Logic.pin1, R_pullup.Pin_0
  GND: D2.anode, C_pin.0
  N2: R_pullup.Pin_1, 5V_2.pin1
