# Fritzing sketch AnaCompMUX (saved by Fritzing 1.0.3b)
breadboards: 1

parts:
  LDR1 = Photocell (LDR) [package=THT]
  R2 = Resistor [tolerance=±5% power=0.25 resistance=10k package=THT]
  R3 = Resistor [tolerance=±5% power=0.25 resistance=560 package=THT]
  LED1 = LED - 5mm [color="Yellow (595nm)" current=0.030 package="5 mm [THT]"]
  VR1 = Trimmer Potentiometer [maximum_resistance=10kΩ knob_status=50% power=0.5W package=THT]
  Part1 = Arduino Uno (Rev3)

nets:
  VCC: LDR1.pin_0, VR1.leg2, Part1.5V
  ADC0: LDR1.pin_1, R2.Pin_1, Part1.A0
  GND: R2.Pin_0, LED1.cathode, VR1.leg1, Part1.GND
  N1: R3.Pin_0, LED1.anode
  D13: R3.Pin_1, Part1.D13/SCK
  AIN0: VR1.wiper, Part1.D6_PWM

notes:
  VR1 allows the "darkness" setting to be varied.
  The LDR and R2 form a voltage divider which is fed into the AIN1 pin as the current light level.
  The LED is lit when the light falls below the preset level.
