# Fritzing sketch Connections (saved by Fritzing 1.0.3b)
breadboards: 1

parts:
  Part2 = Arduino Uno (Rev3)
  LCD1 = LCD screen
  R1 = Resistor [tolerance=±5% power=0.25W resistance=560 package=THT]
  VR1 = Rotary Potentiometer (Small) [maximum_resistance=10k knob_status=50% power=0.5W package=THT]

nets:
  E: Part2.D11_PWM/MOSI, LCD1.E
  RS: Part2.D12/MISO, LCD1.RS
  GND: Part2.GND, LCD1.VSS, LCD1.R/W, LCD1.LED-, VR1.leg1
  DB7: Part2.D2, LCD1.DB7
  DB6: Part2.D3_PWM, LCD1.DB6
  DB5: Part2.D4, LCD1.DB5
  DB4: Part2.D5_PWM, LCD1.DB4
  VCC: Part2.5V, LCD1.VDD, R1.Pin_0, VR1.leg2
  CONTRAST: LCD1.V0, VR1.wiper
  N1: LCD1.LED+, R1.Pin_1

notes:
  D12/RS
  D11/E
  D4--D2
  DB4--DB7
  DB4
  DB7
