# Fritzing sketch SPI_Peripheral (saved by Fritzing 1.0.3b)
breadboards: 1

parts:
  Part1 = Arduino Uno (Rev3)
  R1 = Resistor [tolerance=±5% resistance=560 power=0.25 package=THT]
  R2 = Resistor [tolerance=±5% resistance=560 power=0.25 package=THT]
  LED1 = LED - 5mm [color="Red (633nm)" current=0.030 package="5 mm [THT]"]
  LED2 = LED - 5mm [color="Red (633nm)" current=0.030 package="5 mm [THT]"]
  LED3 = LED - 5mm [color="Red (633nm)" current=0.030 package="5 mm [THT]"]
  LED4 = LED - 5mm [color="Red (633nm)" current=0.030 package="5 mm [THT]"]
  LED5 = LED - 5mm [color="Red (633nm)" current=0.030 package="5 mm [THT]"]
  LED6 = LED - 5mm [color="Red (633nm)" current=0.030 package="5 mm [THT]"]
  LED7 = LED - 5mm [color="Red (633nm)" current=0.030 package="5 mm [THT]"]
  LED8 = LED - 5mm [color="Red (633nm)" current=0.030 package="5 mm [THT]"]
  R3 = Resistor [tolerance=±5% resistance=560 power=0.25 package=THT]
  R4 = Resistor [tolerance=±5% resistance=560 power=0.25 package=THT]
  R5 = Resistor [tolerance=±5% resistance=560 power=0.25 package=THT]
  R6 = Resistor [tolerance=±5% resistance=560 power=0.25 package=THT]
  R7 = Resistor [tolerance=±5% resistance=560 power=0.25 package=THT]
  R8 = Resistor [tolerance=±5% resistance=560 power=0.25 package=THT]
  Part2 = Arduino Uno (Rev3)

nets:
  N1: Part1.D10_PWM/SS, Part2.D10_PWM/SS
  N2: Part1.D11_PWM/MOSI, Part2.D11_PWM/MOSI
  N3: Part1.D12/MISO, Part2.D12/MISO
  N4: Part1.D13/SCK, Part2.D13/SCK
  GND: Part1.GND, LED1.cathode, LED2.cathode, LED3.cathode, LED4.cathode, LED5.cathode, LED6.cathode, LED7.cathode, LED8.cathode, Part2.GND
  N5: Part1.D0/RX, R2.Pin_0
  N6: Part1.D1/TX, R1.Pin_0
  N7: Part1.D2, R3.Pin_0
  N8: Part1.D3_PWM, R4.Pin_0
  N9: Part1.D4, R5.Pin_0
  N10: Part1.D5_PWM, R6.Pin_0
  N11: Part1.D6_PWM, R7.Pin_0
  N12: Part1.D7, R8.Pin_0
  5V: Part1.5V, Part2.5V
  N13: R1.Pin_1, LED7.anode
  N14: R2.Pin_1, LED8.anode
  N15: LED1.anode, R8.Pin_1
  N16: LED2.anode, R7.Pin_1
  N17: LED3.anode, R6.Pin_1
  N18: LED4.anode, R5.Pin_1
  N19: LED5.anode, R4.Pin_1
  N20: LED6.anode, R3.Pin_1

notes:
  GND
  5V
  LED_1 = D7
  LED_2 = D6
  LED_3 = D5
  LED_4 = D4
  LED_5 = D3
  LED_6 = D2
  LED_7 = D1
  LED_8 = D0
  Duemilanove - Controller
  Arduino Uno - Peripheral
  SCK
  MOSI
  MISO
  SS
  NOTE: Power is applied to the Peripheral via 5V and GND pins.
  NOTE: Power is applied to the Controller via USB.
  All resistors are 560R.
