# Fritzing sketch SPI_LEDs_ASM (saved by Fritzing 1.0.3b)
breadboards: 1

parts:
  Part1 = Arduino Uno (Rev3)
  R1 = Resistor [tolerance=±5% resistance=560 power=0.25 package=THT]
  R2 = Resistor [tolerance=±5% resistance=560 power=0.25 package=THT]
  LED1 = LED - 5mm [color="Red (633nm)" current=0.030 package="5 mm [THT]"]
  LED2 = LED - 5mm [color="Red (633nm)" current=0.030 package="5 mm [THT]"]
  LED3 = LED - 5mm [color="Red (633nm)" current=0.030 package="5 mm [THT]"]
  LED4 = LED - 5mm [color="Red (633nm)" current=0.030 package="5 mm [THT]"]
  LED5 = LED - 5mm [color="Red (633nm)" current=0.030 package="5 mm [THT]"]
  LED6 = LED - 5mm [color="Red (633nm)" current=0.030 package="5 mm [THT]"]
  LED7 = LED - 5mm [color="Red (633nm)" current=0.030 package="5 mm [THT]"]
  LED8 = LED - 5mm [color="Red (633nm)" current=0.030 package="5 mm [THT]"]
  U1 = 74HC595 [package="DIP16 [THT]"]
  R3 = Resistor [tolerance=±5% resistance=560 power=0.25 package=THT]
  R4 = Resistor [tolerance=±5% resistance=560 power=0.25 package=THT]
  R5 = Resistor [tolerance=±5% resistance=560 power=0.25 package=THT]
  R6 = Resistor [tolerance=±5% resistance=560 power=0.25 package=THT]
  R7 = Resistor [tolerance=±5% resistance=560 power=0.25 package=THT]
  R8 = Resistor [tolerance=±5% resistance=560 power=0.25 package=THT]
  R9 = Resistor [tolerance=±5% resistance=10k power=0.25 package=THT]
  R10 = Resistor [tolerance=±5% resistance=10k power=0.25 package=THT]

nets:
  D8: Part1.D8, U1.ST_CP
  D9: Part1.D9_PWM, U1.OE, R10.Pin_0
  MOSI/COSI: Part1.D11_PWM/MOSI, U1.DS
  SCK: Part1.D13/SCK, U1.SH_CP
  5V: Part1.5V, U1.VCC, R9.Pin_1, R10.Pin_1
  GND: Part1.GND, LED1.cathode, LED2.cathode, LED3.cathode, LED4.cathode, LED5.cathode, LED6.cathode, LED7.cathode, LED8.cathode, U1.GND
  Q7: R1.Pin_0, U1.Q7
  N1: R1.Pin_1, LED8.anode
  Q6: R2.Pin_0, U1.Q6
  N2: R2.Pin_1, LED7.anode
  N3: LED1.anode, R8.Pin_1
  N4: LED2.anode, R7.Pin_1
  N5: LED3.anode, R6.Pin_1
  N6: LED4.anode, R5.Pin_1
  N7: LED5.anode, R4.Pin_1
  N8: LED6.anode, R3.Pin_1
  Q1: U1.Q1, R7.Pin_0
  Q2: U1.Q2, R6.Pin_0
  Q3: U1.Q3, R5.Pin_0
  Q4: U1.Q4, R4.Pin_0
  Q5: U1.Q5, R3.Pin_0
  N9: U1.MR, R9.Pin_0
  Q0: U1.Q0, R8.Pin_0

notes:
  GND
  5V
  10K pullup/D9/~OE
  10K pullup/~SRCLR
  D13/SCK
  D11/MOSI
  D8/CS
  D9/~OE
  QA - Pin 15
  QB - Pin 1
  QC - Pin 2
  QD - Pin 3
  QE - Pin 4
  QF - Pin 5
  QG - Pin 6
  QH - Pin 7
  Shift Register
  All resistors are 560R.
