# Fritzing sketch LM75A_Read (saved by Fritzing 1.0.3b)
breadboards: 1

parts:
  Part1 = Arduino Uno (Rev3)
  Part2 = Digital Temperature Sensor Breakout - TMP102
  R1 = Resistor [tolerance=±5% resistance=10k power=0.25W package=THT]
  R2 = Resistor [tolerance=±5% resistance=10k power=0.25W package=THT]
  R3 = Resistor [tolerance=±5% power=0.25W resistance=60 package=THT]
  LED1 = LED - 5mm [color="Red (633nm)" current=0.030A package="5 mm [THT]"]

nets:
  N1: Part1.A4/SDA, Part2.SDA, R1.Pin_1
  N2: Part1.A5/SCL, Part2.SCL, R2.Pin_1
  N3: Part1.D13/SCK, R3.Pin_0
  N4: Part1.D2, Part2.ALERT
  N5: Part1.5V, Part2.V+, R1.Pin_0, R2.Pin_0
  GND: Part1.GND, Part2.GND, LED1.cathode
  N6: R3.Pin_1, LED1.anode

notes:
  C1
  GND
  5V
  R1 and R2 are 10K
  R1
  R2
  A4/SDA
  A5/SCL
  D13
  D2
  VCC
  OS
  R3
  R3 is 560R
